// Logisim project MyCpu.circ as structural Verilog: 3 circuits, main circuit main
module main (
  output zero_flag,
  output [7:0] out_a,
  output [7:0] out_b
);

  wire and_2_out, and_3_out, clock_1_out, decoder_1_out0, decoder_1_out1, decoder_1_out2, decoder_1_out3,
       not_1_out, not_2_out, not_3_out, not_4_out, not_5_out, not_6_out, not_7_out, or_2_out, register_1_q;
  wire [7:0] adder_1_out, adder_2_out, and_1_out, bit_extender_1_out, multiplexer_1_out, multiplexer_2_out,
       multiplexer_3_out, multiplexer_4_out, multiplexer_5_out, multiplexer_6_out, or_1_out,
       Program_Counter_q, R0_q, R1_q, R2_q, R3_q, ram_1_data, subtractor_1_out;
  wire [15:0] rom_1_data;

  Clock clock_1 (.out(clock_1_out));
  Register R0 (.D(multiplexer_2_out), .en(decoder_1_out0), .Q(R0_q), .clk(not_1_out));  // open: clr
  not not_1 (not_1_out, clock_1_out);
  not not_2 (not_2_out, clock_1_out);
  Adder adder_1 (.a(multiplexer_3_out), .b(multiplexer_6_out), .out(adder_1_out));  // open: cin, cout
  Subtractor subtractor_1 (.a(multiplexer_3_out), .b(multiplexer_6_out), .out(subtractor_1_out));  // open: bin, bout
  Register R1 (.D(multiplexer_2_out), .en(decoder_1_out1), .Q(R1_q), .clk(not_2_out));  // open: clr
  assign and_1_out = multiplexer_3_out & multiplexer_6_out;  // AND_Gate and_1, 8 bits wide
  assign or_1_out = multiplexer_3_out | multiplexer_6_out;  // OR_Gate or_1, 8 bits wide
  Register R2 (.D(multiplexer_2_out), .en(decoder_1_out2), .Q(R2_q), .clk(not_3_out));  // open: clr
  not not_3 (not_3_out, clock_1_out);
  and and_2 (and_2_out, rom_1_data[15], rom_1_data[14]);
  Register R3 (.D(multiplexer_2_out), .en(decoder_1_out3), .Q(R3_q), .clk(not_4_out));  // open: clr
  not not_4 (not_4_out, clock_1_out);
  Register #(.width(1)) register_1 (.D(zero_flag), .en(and_2_out), .Q(register_1_q), .clk(clock_1_out));  // open: clr
  and and_3 (and_3_out, not_5_out, rom_1_data[14]);
  Multiplexer #(.select(2), .width(8)) multiplexer_1 (
    .in0(adder_1_out), .in1(subtractor_1_out), .in2(and_1_out), .in3(or_1_out), .out(multiplexer_1_out),
    .sel(rom_1_data[15:14]));  // open: en
  not not_5 (not_5_out, rom_1_data[13]);
  Multiplexer #(.width(8), .enable("false")) multiplexer_2 (
    .in0(multiplexer_1_out), .in1(ram_1_data), .out(multiplexer_2_out), .sel(rom_1_data[6]));
  not not_6 (not_6_out, register_1_q);
  Multiplexer #(.select(2), .width(8)) multiplexer_3 (
    .in0(R0_q), .in1(R1_q), .in2(R2_q), .in3(R0_q), .out(multiplexer_3_out), .sel(rom_1_data[10:9]));  // open: en
  Multiplexer #(.select(2), .width(8)) multiplexer_4 (
    .in0(R0_q), .in1(R1_q), .in2(R2_q), .in3(R3_q), .out(multiplexer_4_out), .sel(rom_1_data[8:7]));  // open: en
  Comparator comparator_1 (.a(multiplexer_1_out), .b({8{1'b0}}), .eq(zero_flag));  // open: gt, lt
  or or_2 (or_2_out, not_6_out, rom_1_data[12]);
  Multiplexer #(.width(8), .enable("false")) multiplexer_5 (
    .in0(adder_2_out), .in1(bit_extender_1_out), .out(multiplexer_5_out), .sel(and_3_out));
  Decoder #(.select(2), .disabled(0)) decoder_1 (
    .out0(decoder_1_out0), .out1(decoder_1_out1), .out2(decoder_1_out2), .out3(decoder_1_out3),
    .sel(rom_1_data[13:12]), .en(rom_1_data[11]));
  RAM ram_1 (.addr(multiplexer_1_out), .data(ram_1_data), .sel(1'b1), .clk(clock_1_out), .ld(not_7_out));  // open: clr
  assign ram_1_data = rom_1_data[5] ? multiplexer_4_out : 8'bz;  // Controlled_Buffer controlled_buffer_1
  not not_7 (not_7_out, rom_1_data[5]);
  Register Program_Counter (.D(multiplexer_5_out), .en(1'b1), .Q(Program_Counter_q), .clk(clock_1_out));  // open: clr
  Adder adder_2 (.a(Program_Counter_q), .b(8'h1), .out(adder_2_out));  // open: cin, cout
  Multiplexer #(.width(8), .enable("false")) multiplexer_6 (
    .in0(multiplexer_4_out), .in1(bit_extender_1_out), .out(multiplexer_6_out), .sel(rom_1_data[4]));
  ROM #(.dataWidth(16)) rom_1 (.addr(Program_Counter_q), .data(rom_1_data));  // open: sel
  assign bit_extender_1_out = {{4{1'b0}}, rom_1_data[3:0]};  // Bit_Extender bit_extender_1

  // Notes on the sheet:
  //   contents of rom_1 (hex, n*v repeats v):
  //   85a 1850 2851 1130 811 7019 4012 10b0 5010 43*0 10b0 5010
endmodule

module ALU (
  input  [7:0] A,
  input  [7:0] B,
  input  [1:0] ALU_op,
  output [7:0] Output,
  output zero_flag
);

  wire [7:0] adder_1_out, and_1_out, or_1_out, subtractor_1_out;

  Adder adder_1 (.a(A), .b(B), .out(adder_1_out));  // open: cin, cout
  Subtractor subtractor_1 (.a(A), .b(B), .out(subtractor_1_out));  // open: bin, bout
  assign and_1_out = A & B;  // AND_Gate and_1, 8 bits wide
  assign or_1_out = A | B;  // OR_Gate or_1, 8 bits wide
  Multiplexer #(.select(2), .width(8)) multiplexer_1 (
    .in0(adder_1_out), .in1(subtractor_1_out), .in2(and_1_out), .in3(or_1_out), .out(Output), .sel(ALU_op));  // open: en
  Comparator comparator_1 (.a(Output), .b({8{1'b0}}), .eq(zero_flag));  // open: gt, lt
endmodule

module Register_File (
  input  [7:0] Write_Data,
  input  [1:0] write_adress,
  input  [1:0] Read_A,
  input  [1:0] Read_B,
  input  enable_write,
  output [7:0] out_a,
  output [7:0] out_b
);

  wire clock_1_out, decoder_1_out0, decoder_1_out1, decoder_1_out2, decoder_1_out3;
  wire [7:0] multiplexer_1_out, multiplexer_2_out, R0_q, R1_q, R2_q, R3_q;

  Clock clock_1 (.out(clock_1_out));
  Register R0 (.D(Write_Data), .Q(R0_q), .clk(clock_1_out), .clr(decoder_1_out0));  // open: en
  Register R1 (.D(Write_Data), .Q(R1_q), .clk(clock_1_out), .clr(decoder_1_out1));  // open: en
  Register R2 (.D(Write_Data), .Q(R2_q), .clk(clock_1_out), .clr(decoder_1_out2));  // open: en
  Register R3 (.D(Write_Data), .Q(R3_q), .clk(clock_1_out), .clr(decoder_1_out3));  // open: en
  Multiplexer #(.select(2), .width(8)) multiplexer_1 (
    .in0(R0_q), .in1(R1_q), .in2(R2_q), .in3(R0_q), .out(multiplexer_1_out), .sel(Read_A));  // open: en
  Multiplexer #(.select(2), .width(8)) multiplexer_2 (
    .in0(R0_q), .in1(R1_q), .in2(R2_q), .in3(R3_q), .out(multiplexer_2_out), .sel(Read_B));  // open: en
  Decoder #(.select(2)) decoder_1 (
    .out0(decoder_1_out0), .out1(decoder_1_out1), .out2(decoder_1_out2), .out3(decoder_1_out3),
    .sel(write_adress), .en(enable_write));
endmodule
